// Digital circuit DataMemory.dig as structural Verilog
module DataMemory (
  input  dmwen,
  input  [31:0] addr,
  input  load,
  input  [31:0] func3,
  input  [31:0] wdata,
  input  clock,
  output [31:0] out,
  output [31:0] outf3
);

  wire and_1_out, and_2_out, and_3_out, and_4_out, comparator_1_eq, comparator_2_eq, comparator_3_eq,
       or_1_out, or_2_out;

  Comparator #(.Bits(32)) comparator_1 (.a(32'h2), .b(func3), .eq(comparator_1_eq));  // open: gt, lt
  Comparator #(.Bits(32)) comparator_2 (.a(32'h1), .b(func3), .eq(comparator_2_eq));  // open: gt, lt
  Comparator #(.Bits(32)) comparator_3 (.a({32{1'b0}}), .b(func3), .eq(comparator_3_eq));  // open: gt, lt
  and and_1 (and_1_out, dmwen, or_1_out);
  or or_1 (or_1_out, comparator_1_eq, comparator_2_eq, comparator_3_eq);
  BlockRAMDualPort #(.AddrBits(24), .Bits(8)) byte0 (
    .A(addr[23:0]), .Din(wdata[7:0]), .str(and_1_out), .C(clock), .D(out[7:0]));
  or or_2 (or_2_out, comparator_1_eq, comparator_2_eq);
  and and_2 (and_2_out, dmwen, or_2_out);
  BlockRAMDualPort #(.AddrBits(24), .Bits(8)) byte1 (
    .A(addr[23:0]), .Din(wdata[15:8]), .str(and_2_out), .C(clock), .D(out[15:8]));
  and and_3 (and_3_out, dmwen, comparator_1_eq);
  BlockRAMDualPort #(.AddrBits(24), .Bits(8)) byte2 (
    .A(addr[23:0]), .Din(wdata[23:16]), .str(and_3_out), .C(clock), .D(out[23:16]));
  BlockRAMDualPort #(.AddrBits(24), .Bits(8)) byte3 (
    .A(addr[23:0]), .Din(wdata[31:24]), .str(and_4_out), .C(clock), .D(out[31:24]));
  and and_4 (and_4_out, dmwen, comparator_1_eq);
  Multiplexer #(.Bits(8)) multiplexer_1 (
    .sel(comparator_1_eq), .in_0({8{1'b0}}), .in_1(out[31:24]), .out(outf3[31:24]));
  Multiplexer #(.Bits(8)) multiplexer_2 (
    .sel(comparator_1_eq), .in_0({8{1'b0}}), .in_1(out[23:16]), .out(outf3[23:16]));
  Multiplexer #(.Bits(8)) multiplexer_3 (.sel(or_2_out), .in_0({8{1'b0}}), .in_1(out[15:8]), .out(outf3[15:8]));
  Multiplexer #(.Bits(8)) multiplexer_4 (.sel(or_1_out), .in_0({8{1'b0}}), .in_1(out[7:0]), .out(outf3[7:0]));
endmodule
