// Digital circuit ProgramMemory.dig as structural Verilog
module ProgramMemory (
  input  [31:0] addr,
  output [31:0] inst
);

  wire [23:0] add_1_s, add_2_s, add_3_s;

  ROM #(.AddrBits(24), .Bits(8)) Progmem (.A(addr[23:0]), .sel(1'b1), .D(inst[31:24]));
  Add #(.Bits(24)) add_1 (.a(addr[23:0]), .b(24'h1), .c_i(1'b0), .s(add_1_s));  // open: c_o
  Add #(.Bits(24)) add_2 (.a(add_1_s), .b(24'h1), .c_i(1'b0), .s(add_2_s));  // open: c_o
  ROM #(.AddrBits(24), .Bits(8)) rom_1 (.A(add_1_s), .sel(1'b1), .D(inst[23:16]));
  Add #(.Bits(24)) add_3 (.a(add_2_s), .b(24'h1), .c_i(1'b0), .s(add_3_s));  // open: c_o
  ROM #(.AddrBits(24), .Bits(8)) rom_2 (.A(add_2_s), .sel(1'b1), .D(inst[15:8]));
  ROM #(.AddrBits(24), .Bits(8)) rom_3 (.A(add_3_s), .sel(1'b1), .D(inst[7:0]));
endmodule
