// Digital circuit alu.dig as structural Verilog
module alu (
  input  [31:0] arg1,
  input  [31:0] arg2,
  input  [2:0] f3,
  input  f9,
  output out
);

  wire multiplexer_1_out, multiplexer_2_out, slt_lt, sltu_lt;
  wire [31:0] add, \and , \or , sll, sra, srl, sub, \xor ;
  wire [31:1] slt, sltu;

  Add #(.Bits(32)) add_1 (.a(arg1), .b(arg2), .c_i(1'b0), .s(add));  // open: c_o
  Sub #(.Bits(32)) sub_1 (.a(arg1), .b(arg2), .c_i(1'b0), .s(sub));  // open: c_o
  assign \xor  = arg1 ^ arg2;  // XOr xor_1, 32 bits wide
  assign \or  = arg1 | arg2;  // Or or_1, 32 bits wide
  assign \and  = arg1 & arg2;  // And and_1, 32 bits wide
  BarrelShifter #(.Bits(32)) u_sll (.in(arg1), .shift(arg2[5:0]), .out(sll));
  BarrelShifter #(.Bits(32), .direction("right")) u_srl (.in(arg1), .shift(arg2[5:0]), .out(srl));
  BarrelShifter #(.barrelShifterMode("arithmetic"), .Bits(32)) u_sra (.in(arg1), .shift(arg2[5:0]), .out(sra));
  Comparator #(.Signed("true"), .Bits(32)) u_slt (.a(arg1), .b(arg2), .lt(slt_lt));  // open: gt, eq
  Comparator #(.Bits(32)) u_sltu (.a(arg1), .b(arg2), .lt(sltu_lt));  // open: gt, eq
  Multiplexer multiplexer_1 (.sel(f3[0]), .in_0(add[0]), .in_1(sub[0]), .out(multiplexer_1_out));
  Multiplexer multiplexer_2 (.sel(f9), .in_0(sra[0]), .in_1(srl[0]), .out(multiplexer_2_out));
  Multiplexer #(.Selector_Bits(3)) multiplexer_3 (
    .sel(f3), .in_0(multiplexer_1_out), .in_1(sll[0]), .in_2(1'b0), .in_3(1'b0), .in_4(\xor [0]),
    .in_5(multiplexer_2_out), .in_6(\or [0]), .in_7(\and [0]), .out(out));
  // Probe bin on out
  // Probe dec on out
  // Probe hex on out
  // Pins of 1 and 3 bits meet at f3
  // Pins of 1 and 32 bits meet at add
  // Pins of 1 and 32 bits meet at sub
  // Pins of 1 and 32 bits meet at \xor 
  // Pins of 1 and 32 bits meet at \or 
  // Pins of 1 and 32 bits meet at \and 
  // Pins of 1 and 32 bits meet at sll
  // Pins of 1 and 32 bits meet at srl
  // Pins of 1 and 32 bits meet at sra
  // Pins of 1 and 32 bits meet at {sltu, 1'b0}
  // Pins of 1 and 32 bits meet at {sltu, 1'b0}
  // Pins of 1 and 32 bits meet at {slt, 1'b0}
endmodule
