// Digital circuit cann-registerfile_tb.dig as structural Verilog
module cann_registerfile_tb (
  input  [4:0] rs1,
  input  [4:0] rs2,
  input  [4:0] rd,
  input  Clock,
  input  enable,
  input  [31:0] data,
  output [31:0] rs1Data,
  output [31:0] rs1Data_2
);

  cann_registerfile cann_registerfile_1 (
    .rfwrenable(enable), .rdAdrs(rd), .rdData(data), .rs1Adrs(rs1), .rs2Adrs(rs2), .clock(Clock),
    .rs1Data(rs1Data), .rs2Data(rs1Data_2));
endmodule
