// Digital circuit instdecoder.dig as structural Verilog
module instdecoder (
  input  [31:0] Inst,
  output [6:0] Opcode,
  output [4:0] Rd,
  output [4:0] Rs1,
  output [4:0] Rs2,
  output [2:0] Funct3,
  output [6:0] Funct7,
  output [11:0] Imm
);


  assign Funct3 = Inst[14:12];
  assign Funct7 = Inst[31:25];
  assign Imm = Inst[31:20];
  assign Opcode = Inst[6:0];
  assign Rd = Inst[11:7];
  assign Rs1 = Inst[19:15];
  assign Rs2 = Inst[24:20];
endmodule
