// Digital circuit main.dig as structural Verilog
module main (
  input  reset
);

  wire add_1_s, alu, brinst, cann_registerfile_1_p8, clock, datamemory_1_p4, deq, dge, dgeu, dlt, dltu,
       dmwen, jal_jair, multiplexer_2_out, multiplexer_3_out, notconnected_1_out, pc, pc_jump, rd1, rdest,
       rfwren, rs1_pc;
  wire [1:0] wbsel;
  wire [4:0] rd, rs1, rs2;
  wire [31:0] inst;

  Multiplexer multiplexer_1 (.sel(pc_jump), .in_0(add_1_s), .in_1(alu));  // open: out
  Add add_1 (.a(pc), .b(1'b0), .c_i(1'b0), .s(add_1_s));  // open: c_o
  // ProgramMemory programmemory_1: pin names not known; wires that end beside it: pc, inst
  instdecoder instdecoder_1 (.Inst(inst), .Rd(rd), .Rs1(rs1), .Rs2(rs2));  // open: Opcode, Funct3, Funct7, Imm
  // cann_registerfile cann_registerfile_1: pin names not known; wires that end beside it: rfwren, rd, rdest, rs1, rs2, clock, rd1, cann_registerfile_1_p8
  // branch branch_1: pin names not known; wires that end beside it: rd1, cann_registerfile_1_p8, brinst, jal_jair, rs1_pc, pc_jump, deq, dlt, dge, dltu, dgeu
  Multiplexer multiplexer_2 (.in_0(cann_registerfile_1_p8), .out(multiplexer_2_out));  // open: sel, in_1
  Multiplexer multiplexer_3 (.sel(rs1_pc), .in_0(rd1), .in_1(pc), .out(multiplexer_3_out));
  Button button_1 (.out(clock));
  // alu alu_1: pin names not known; wires that end beside it: multiplexer_3_out, multiplexer_2_out, alu
  // DataMemory datamemory_1: pin names not known; wires that end beside it: dmwen, alu, clock, datamemory_1_p4
  Multiplexer #(.Selector_Bits(2)) multiplexer_4 (
    .sel(wbsel), .in_0(alu), .in_1(datamemory_1_p4), .in_2(add_1_s), .in_3(notconnected_1_out), .out(rdest));
  // NotConnected on notconnected_1_out
  // Pins of 1 and 32 bits meet at 32'h4
  // Pins of 1 and 32 bits meet at {32{1'b0}}
endmodule
